# Fritzing sketch SiKoGen (saved by Fritzing 0.9.2b)
breadboards: 1

parts:
  IC1 = 3W33DC15DC [package=DIL]
  R1 = Resistor [tolerance=±5% resistance=1k package=THT]
  R2 = Resistor [tolerance=±5% resistance=1k package=THT]
  IC2 = 3W33DC15DC [package=DIL]
  VCC1 = Battery

nets:
  N1: IC1.VIN, VCC1.+
  N2: IC1.GND#4, VCC1.-
  N3: IC1.+Vo, R2.Pin_1, IC2.VIN
  N4: IC1.-Vo, R1.Pin_0
  N5: R1.Pin_1, R2.Pin_0, IC2.GND#4
